# Fritzing sketch Board (saved by Fritzing 0.9.3b)
perfboards: 1

parts:
  Part1 = Arduino Pro Mini v13
  VCC1 = Battery block 9V
  LED1 = RGB LED (com. cathode, rgb) [package="5 mm [THT]"]
  S1 = Round Pushbutton
  J1 = Piezo Speaker

nets:
  N1: Part1.GND, VCC1.-, LED1.common_cathode, J1.pin1
  N2: Part1.VCC, VCC1.+
  N3: Part1.D9_PWM, S1.leg0
  N4: Part1.D8, S1.leg1
  N5: Part1.D7, J1.pin2
  N6: Part1.D4, LED1.red_anode
  N7: Part1.D2, LED1.green_anode
